# Fritzing sketch Schematic (saved by Fritzing 0.9.5d)

parts:
  Driver1 = 28BYJ-48 Driver Module [part_number=ULN2003 package=THT]
  SM1 = 28BYJ-48 Stepper Motor [part_number=28BYJ-48]
  Part1 = Arduino Uno (Rev3) - ICSP
  BAT1 = BC9VPC [package=bc9vpc]

nets:
  N1: Driver1.IN1, Part1.D12/MISO
  N2: Driver1.IN2, Part1.D11_PWM/MOSI
  N3: Driver1.IN3, Part1.D10_PWM/SS
  N4: Driver1.IN4, Part1.D9_PWM
  GND: Driver1.GND, Part1.GND, BAT1.V-
  N5: Driver1.Vmotor, BAT1.V+
  N6: Driver1.blue-pin, SM1.blue-pin
  N7: Driver1.pink-pin, SM1.pink-pin
  N8: Driver1.yellow-pin, SM1.yellow-pin
  N9: Driver1.orange-pin, SM1.orange-pin
  N10: Driver1.red-pin, SM1.red-pin

custom parts:
  28BYJ-48 Driver Module: High-power ULN2003 Stepper Motor Driver Board Test Module For Arduino AVR SMD
  28BYJ-48 Stepper Motor: Unipolar Stepper Motor 28BYJ-48 Top coil - pink & orange Bottom coil - blue & yellow Common rail - red Connector pins: blue - pink - yellow - orange - red
